# Fritzing sketch projectfzz (saved by Fritzing 0.9.3b)
circuit board: 8.46667cm x 5.64444cm
breadboards: 1

parts:
  YL-83_-_Control_Board1 = YL-83 Rain Sensor - Control Board
  M1 = ESP32-S3-DevKitC-1-N8R8-v1 [part_number=ESP32-S3-DevKitC-1-N8R8-v1]
  YL-83_-_Detection_Board1 = YL-83 Rain Sensor - Detection Board
  M2 = fc-51 [package=THT]
  Part1 = LCD1602-I2C
  J1 = Basic Servo
  J2 = Basic Servo
  R1 = Photocell (LDR) [package=THT]
  LED1 = LED - 5mm [color="Green (565nm)" package="5 mm [THT]"]
  LED2 = LED - 5mm [color="Red (633nm)" package="5 mm [THT]"]
  U1 = GAS_SENSOR [package=mq-3]
  R2 = Resistor [tolerance=±5% resistance=220 package="0603 [SMD]"]
  Keypad4x1 = Keypad Membran 4x4
  J3 = Piezo Speaker

nets:
  VCC: YL-83_-_Control_Board1.VCC, M1.pin_1, M1.pin_2, M2.pin3, Part1.VCC, U1.H2
  GND: YL-83_-_Control_Board1.GND, M1.pin_22, M1.pin_24, M1.pin_44, M2.pin2, Part1.GND, Part1.SCL, J1.gnd, J2.gnd, LED1.cathode, LED2.cathode, U1.H1, R2.Pin_1, J3.pin1
  N1: YL-83_-_Control_Board1.DO, M1.pin_26
  N2: YL-83_-_Control_Board1.POS, YL-83_-_Detection_Board1.POS
  N3: YL-83_-_Control_Board1.NEG, YL-83_-_Detection_Board1.NEG
  N4: M1.pin_6, Keypad4x1.Pin8
  N5: M1.pin_7, Keypad4x1.Pin7
  N6: M1.pin_8, Keypad4x1.Pin6
  N7: M1.pin_9, Keypad4x1.Pin5
  N8: M1.pin_10, Keypad4x1.Pin4
  N9: M1.pin_11, Keypad4x1.Pin3
  N10: M1.pin_12, Keypad4x1.Pin2
  N11: M1.pin_13, Keypad4x1.Pin1
  N12: M1.pin_20, U1.B1
  VCC_2: M1.pin_21, J1.vcc, J2.vcc, R1.pin_0
  N13: M1.pin_25, Part1.SDA
  N14: M1.pin_34, M2.pin1
  N15: M1.pin_35, R1.pin_1, R2.Pin_0

custom parts:
  YL-83 Rain Sensor - Control Board: The YL-83 is a rain sensor that has more resistance when dry and less resistance when wet. The module runs at 5V.
  ESP32-S3-DevKitC-1-N8R8-v1: ESP32-S3-DevKitC-1-N8R8-v1 This module is 44pins long (2x22) and 11 pins width.
  YL-83 Rain Sensor - Detection Board: The YL-83 is a rain sensor that has more resistance when dry and less resistance when wet. The module runs at 5V.
  LCD1602-I2C: A standard character display, usually with 2x16 characters. Comes in many colors with LCM1602 IIC attached.
  Keypad Membran 4x4: Membrane Keypad 4x4 Matrix
